# Fritzing sketch l293d_with_two_dc_motors (saved by Fritzing 0.9.3b)
breadboards: 1

parts:
  IC1 = L293D [package=THT]
  Raspberry_Pi_1 = Raspberry Pi 3 [part_number=RPI-3-V1.2]
  VCC1 = Battery block 9V
  M1 = DC Motor
  M2 = DC Motor

nets:
  N1: IC1.Enable_1, Raspberry_Pi_1.GIPO25
  N2: IC1.In_1, Raspberry_Pi_1.GIPO24
  N3: IC1.Out_1_(_Controlled_by_Enable_1_), M1.pin_2
  N4: IC1.0V, Raspberry_Pi_1.GND, VCC1.-
  N5: IC1.Out_2_(_Controlled_by_Enable_1_), M1.pin_1
  N6: IC1.In_2, Raspberry_Pi_1.GIPO23
  N7: IC1.+Vmotor, VCC1.+
  N8: IC1.Enable_2, Raspberry_Pi_1.GIPO16
  N9: IC1.In_3, Raspberry_Pi_1.GIPO20
  N10: IC1.Out_3_(_Controlled_by_Enable_2_), M2.pin_2
  N11: IC1.Out_4_(_Controlled_by_Enable_2_), M2.pin_1
  N12: IC1.In_4, Raspberry_Pi_1.GIPO21
  N13: IC1.+V, Raspberry_Pi_1.5V
